# Fritzing sketch Device (saved by Fritzing 0.9.3b)

parts:
  WeMos_D1_Mini1 = WeMos D1 Mini
  IR1 = TSOP312.., 314.. [package=THT]

nets:
  N1: WeMos_D1_Mini1.D6, IR1.GND
  N2: WeMos_D1_Mini1.D8, IR1.Data

notes:
  Ground => D6
  Signal => D8
