# Fritzing sketch Possible_upgrade (saved by Fritzing 0.9.3b)
breadboards: 1

parts:
  WeMos_D1_Mini1 = WeMos D1 Mini
  LED1 = LEDs [package=led10mm]
  Q1 = TRANSISTOR_NPN [package=to-92-ammo]
  R1 = Resistor [tolerance=±5% resistance=1k package=THT]

nets:
  N1: WeMos_D1_Mini1.3V3, LED1.A
  N2: WeMos_D1_Mini1.D7, R1.Pin_0
  N3: WeMos_D1_Mini1.G, Q1.E
  N4: LED1.C, Q1.C
  N5: Q1.B, R1.Pin_1
